// Logisim project circuito.circ as structural Verilog: 1 circuit, main circuit main
module main (
  input  A,
  input  B,
  output out_3,
  output out_4,
  output out_5,
  output out_6,
  output out_7
);

  wire and_1_out, and_2_out, not_1_out, not_3_out, not_4_out, or_1_out, or_2_out;

  not not_1 (not_1_out, A);
  and and_1 (and_1_out, A, A, B);
  not not_2 (out_3, not_1_out);
  not not_3 (not_3_out, and_1_out);
  not not_4 (not_4_out, or_1_out);
  or or_1 (or_1_out, A, B);
  not not_5 (out_6, and_2_out);
  and and_2 (and_2_out, A, B);
  or or_2 (or_2_out, A, B);
  not not_6 (out_7, or_2_out);
  not not_7 (out_4, not_3_out);
  not not_8 (out_5, not_4_out);
endmodule
